# Fritzing sketch BreadBoardWeatherStation (saved by Fritzing 0.9.2b)
breadboards: 1

parts:
  Part1 = Arduino Pro Mini v13
  VCC2 = Battery block 9V
  LED1 = LED - 5mm [color="Red (633nm)" package="5 mm [THT]"]

nets:
  N1: Part1.GND, VCC2.-, LED1.cathode
  N2: Part1.RAW, VCC2.+, LED1.anode
